# Fritzing sketch ILI9225 (saved by Fritzing 0.9.3b)
breadboards: 1

parts:
  U1 = lolin
  LCD1 = TFT 1.8 inch 160x128 w SD

nets:
  N1: U1.connector14, LCD1.pin_8
  N2: U1.connector15, LCD1.pin_7
  N3: U1.connector18, LCD1.pin2
  N4: U1.connector19, LCD1.pin3
  N5: U1.connector26, LCD1.pin_1
  N6: U1.connector27, LCD1.pin_5
  N7: U1.connector28, LCD1.pin4

notes:
  This is not 1.8 but 2.0" in real testing and it is ILI9225
  Medical Signals Box project
  Developed by Walid Amriou
  2019 
  
  Test of ILI9225 by ESP32 - LOLIN32

custom parts:
  TFT 1.8 inch 160x128 w SD: This is a generic 1.8 tft spi lcd display available on ebay and others. The 1.8" display has 128x160 color pixels.

// code stored in the sketch: ILI9225.ino
/*
 
Medical Signals Box project
Developed by Walid Amriou
2019 

Test of ILI9225 by ESP32 - LOLIN32
*/

#include "SPI.h"
#include "TFT_22_ILI9225.h"

#define TFT_CLK 18  // SCK
#define TFT_SDI 23  // SDA
#define TFT_RS  2   // RS
#define TFT_RST 15   // RST
#define TFT_CS  5  // CS
#define TFT_LED 0   // Già collegato a +5V/+3.3V

// Use hardware SPI (faster)
TFT_22_ILI9225 tft = TFT_22_ILI9225(TFT_RST, TFT_RS, TFT_CS, TFT_LED);

const unsigned char gImage_ic[3872] PROGMEM = {/*add image hex here*/};

String duration;
unsigned long startTime;
// Setup
void setup() {
  tft.begin();
  Serial.begin(9600);
}

// Loop
void loop() {
  startTime = millis();
  //tft.drawBitmap(0, 0, gImage_ic, 176, 176, COLOR_CYAN);
  tft.setBackgroundColor(COLOR_BLACK);
  tft.setFont(Terminal6x8);
  tft.drawText(0, 178, "www.walidamriou.com", COLOR_CYAN);
  tft.drawText(0, 188, "Test of ILI9225 176x220 TFT screen", COLOR_GREEN);
  tft.drawText(0, 198, "SPI faster", COLOR_YELLOW);
  duration = String(millis() - startTime);
  tft.drawText(0, 208, duration, COLOR_WHITE);
  while (true);

}
